# Fritzing sketch Alarma (saved by Fritzing 0.9.3b)
circuit board: 8.46667cm x 5.64444cm
breadboards: 1

parts:
  WeMos_D1_R1 = WeMos D1 R2
  Reloj = DS3231MZ Real Time Clock
  SD_CARD_Reader = MicroSD Card Module
  PIR1 = PIR sensor

nets:
  N1: WeMos_D1_R1.D0/RX, WeMos_D1_R1.(D5)
  N2: WeMos_D1_R1.D2, PIR1.SIG
  N3: WeMos_D1_R1.D3, Reloj.sda
  N4: WeMos_D1_R1.D10, SD_CARD_Reader.CS
  N5: WeMos_D1_R1.D11, SD_CARD_Reader.MOSI
  N6: WeMos_D1_R1.D12, SD_CARD_Reader.MISO
  N7: WeMos_D1_R1.D13, SD_CARD_Reader.SCK
  GND: WeMos_D1_R1.GND, Reloj.gnd, SD_CARD_Reader.GND, PIR1.GND
  VCC: WeMos_D1_R1.5V, WeMos_D1_R1.3.3V, Reloj.vcc, SD_CARD_Reader.VCC, PIR1.VDD

custom parts:
  WeMos D1 R2: The D1 R2 is a mini wifi board based on the ESP-8266EX.
  DS3231MZ Real Time Clock: DS3231MZ Real Time Clock. SO-8 surface mount version.
